# Fritzing sketch 1Схема манипулатора (saved by Fritzing 0.9.3b)
circuit board: 1.98853cm x 5.33255cm
circuit board: 5.57666cm x 8.09548cm
stripboards: 1

parts:
  Часть1 = Arduino Nano (Rev3.0)
  J3 = Basic Servo
  J4 = Basic Servo
  J2 = Basic Servo
  J1 = Basic Servo
  J5 = Basic Servo
  J6 = Basic Servo
  J7 = Basic Servo
  J8 = Basic Servo
  Часть2 = Arduino Uno (Rev3)

nets:
  N1: Часть1.D2, J1.pulse
  N2: Часть1.D3, J3.pulse
  N3: Часть1.D4, J2.pulse
  N4: Часть1.D5, J4.pulse
  GND: Часть1.GND, J3.gnd, J4.gnd, J2.gnd, J1.gnd
  VCC: Часть1.5V, J3.vcc, J4.vcc, J2.vcc, J1.vcc
  GND_2: J5.gnd, J6.gnd, J7.gnd, J8.gnd, Часть2.GND
  VCC_2: J5.vcc, J6.vcc, J7.vcc, J8.vcc, Часть2.5V
  N5: J5.pulse, Часть2.D3_PWM
  N6: J6.pulse, Часть2.D5_PWM
  N7: J7.pulse, Часть2.D2
  N8: J8.pulse, Часть2.D4
