# Fritzing sketch Схема манипулатора (saved by Fritzing 0.9.3b)
circuit board: 2.05438cm x 5.59125cm
stripboards: 1

parts:
  Часть1 = Arduino Nano (Rev3.0)
  J3 = Basic Servo
  J4 = Basic Servo
  J2 = Basic Servo
  J1 = Basic Servo

nets:
  GND: Часть1.GND, J3.gnd, J4.gnd, J2.gnd, J1.gnd
  N1: Часть1.D2, J1.pulse
  N2: Часть1.D3, J3.pulse
  N3: Часть1.D4, J2.pulse
  N4: Часть1.D5, J4.pulse
  VCC: Часть1.5V, J3.vcc, J4.vcc, J2.vcc, J1.vcc
